# Fritzing sketch circuit (saved by Fritzing 0.9.4)

parts:
  Mod1 = Raspberry Pi 4B
  Piezo_buzzer1 = Piezo Buzzer

nets:
  N1: Mod1.GND, Piezo_buzzer1.pin_2
  N2: Mod1.GPIO20, Piezo_buzzer1.pin_1

custom parts:
  Piezo Buzzer: Piezo buzzer PS1420P02CT
